// Logisim project main.circ as structural Verilog
module reg_16b (
  input  [15:0] Data,
  input  Input_Enable,
  input  Output_Enable,
  input  Clear,
  input  Clock,
  output [15:0] Output
);

  wire and_1_out;
  wire [15:0] register_1_q;

  and and_1 (and_1_out, Input_Enable, ~Clock);  // AND_Gate
  Register #(.width(16)) register_1 (.D(Data), .en(and_1_out), .Q(register_1_q), .clk(and_1_out), .clr(Clear));
  assign Output = Output_Enable ? register_1_q : 16'bz;  // Controlled_Buffer controlled_buffer_1

  // Notes on the sheet:
  //   General purpose 16bit register
endmodule
